# Fritzing sketch Circuit (saved by Fritzing 0.9.5d)

parts:
  BAT1 = BC9VPC [package=bc9vpc]
  BAT2 = BC9VPC [package=bc9vpc]
  S1 = H-Bridge with L298N
  S2 = Toggle Switch [package=THT]
  S3 = Toggle Switch [package=THT]
  M1 = DC Motor
  Parça2 = Bluetooth HC-05 Macho
  microSD1 = MicroSD Card Module
  Parça1 = Arduino Uno (Rev3)
  AMP1 = PAM8403 6W Stereo Amplifier
  SP1 = SPEAKER [package=pcb_mount_speaker]

nets:
  N1: BAT1.V+, S2.COM
  N2: BAT2.V+, S3.COM
  N3: BAT2.V-, S1.GND
  N4: S1.12V, S3.L2
  N5: S1.IN3, Parça1.D7
  N6: S1.IN4, Parça1.D6_PWM
  N7: S1.ENB, S1.ENB-5V
  N8: S1.M2-01, M1.pin_2
  N9: S1.M2-02, M1.pin_1
  N10: S2.L1, Parça1.VIN
  N11: Parça2.TXD, Parça1.D0/RX
  N12: Parça2.RXD, Parça1.D1/TX
  VCC: Parça2.VCC, Parça1.5V
  GND: microSD1.GND, Parça1.GND
  N13: microSD1.MISO, Parça1.D12/MISO
  N14: microSD1.MOSI, Parça1.D11_PWM/MOSI
  N15: microSD1.SCK, Parça1.D13/SCK
  N16: microSD1.CS, Parça1.D10_PWM/SS
  N17: Parça1.D9_PWM, AMP1.INPUTL
  N18: AMP1.LOUT+, SP1.-
  N19: AMP1.LOUT-, SP1.+

notes:
  L298N toggle switch
  UNO toggle switch
  HC-05 Bluetooth Module
  Micro SD Card Reader:
  (1): GND
  (2): VCC
  (3): MISO
  (4): MOSI
  (5): SCK
  (6): CS
  I use PAM8403 in this project. You can use any amplifier for increase speaker sound.
  And if you using PAM8403 too you can connect two speakers.

custom parts:
  H-Bridge with L298N: h-bridge
  PAM8403 6W Stereo Amplifier: PAM8403 6 Watt Stereo Amplifier
